# Fritzing sketch led5sw1_schema (saved by Fritzing 0.9.5d)
breadboards: 1

parts:
  LED1 = LED - 3mm [color="Red (633nm)" package="3 mm [THT]"]
  LED2 = LED - 3mm [color="Red (633nm)" package="3 mm [THT]"]
  LED3 = LED - 3mm [color="Red (633nm)" package="3 mm [THT]"]
  LED4 = LED - 3mm [color="Red (633nm)" package="3 mm [THT]"]
  LED5 = LED - 3mm [color="Red (633nm)" package="3 mm [THT]"]
  R2 = Resistor [tolerance=±5% resistance=220 package=THT]
  R3 = Resistor [tolerance=±5% resistance=220 package=THT]
  R4 = Resistor [tolerance=±5% resistance=220 package=THT]
  R5 = Resistor [tolerance=±5% resistance=220 package=THT]
  R6 = Resistor [tolerance=±5% resistance=220 package=THT]
  Raspberry_Pi_1 = Raspberry Pi 3 [part_number=RPI-3-V1.2]
  S2 = Pushbutton [package="[THT]"]

nets:
  N1: LED1.cathode, R2.Pin_1
  N2: LED1.anode, Raspberry_Pi_1.GPIO26
  N3: LED2.cathode, R3.Pin_1
  N4: LED2.anode, Raspberry_Pi_1.GPIO19
  N5: LED3.cathode, R4.Pin_1
  N6: LED3.anode, Raspberry_Pi_1.GPIO13
  N7: LED4.cathode, R5.Pin_1
  N8: LED4.anode, Raspberry_Pi_1.GPIO6
  N9: LED5.cathode, R6.Pin_1
  N10: LED5.anode, Raspberry_Pi_1.GPIO5
  N11: R2.Pin_0, R3.Pin_0, R4.Pin_0, R5.Pin_0, R6.Pin_0, Raspberry_Pi_1.GND, S2.Pin_1, S2.Pin_2
  N12: Raspberry_Pi_1.GPIO4, S2.Pin_3, S2.Pin_4
